// Logisim project sCPU.circ as structural Verilog: 2 circuits, main circuit main
module main (
);

  wire clock_1_out, clock_2_out, op_add, op_bner0, op_li, reset;
  wire [1:0] op_code, rd, rs1, rs2;
  wire [3:0] addr, imm;
  wire [7:0] CMD, PC;

  Clock clock_1 (.out(clock_1_out));
  Counter counter_1 (.clr(reset), .clk(clock_1_out), .Q(PC));  // open: load, up, count, D, carry
  Button button_1 (.out(reset));
  OP_Seperator op_seperator_1 (.op(CMD), .op_code(op_code), .rd(rd), .addr(addr), .rs1(rs1), .imm(imm), .rs2(rs2));
  // Probe on PC
  Clock clock_2 (.out(clock_2_out));
  RAM ram_1 (.addr(PC), .oe(1'b1), .clk(clock_2_out), .dout(CMD));  // open: we, din
  Decoder #(.select(2)) decoder_1 (.out0(op_add), .out2(op_li), .out3(op_bner0), .sel(op_code));  // open: out1, en
  Register R0 ();  // open: D, en, clk, Q, clr
  Register R1 ();  // open: D, en, clk, Q, clr
  Register R2 ();  // open: D, en, clk, Q, clr
  Register R3 ();  // open: D, en, clk, Q, clr
  // Probe on CMD
endmodule

module OP_Seperator (
  input  [7:0] op,
  output [1:0] op_code,
  output [1:0] rd,
  output [3:0] addr,
  output [1:0] rs1,
  output [3:0] imm,
  output [1:0] rs2
);


  assign addr = op[5:2];
  assign imm = op[3:0];
  assign op_code = op[7:6];
  assign rd = op[5:4];
  assign rs1 = op[3:2];
  assign rs2 = op[1:0];
endmodule
